# Fritzing sketch EFP_SCHEMATIC (saved by Fritzing 1.0.4)
breadboards: 1

parts:
  Part1 = Arduino Mega 2560 (Rev3)
  SP1 = SPEAKER [package=pcb_mount_speaker]
  VCC1 = 4 x AAA Battery Mount [internal_resistance=0.1Ω]
  C2 = Capacitor Polarized [package=cpol-radial-10uf-25v]
  M1 = PAM8403 Stereo Amplifier with Volume Control [part_number=HW-012]
  R1 = Rotary Potentiometer (Small) [maximum_resistance=10kΩ knob_status=50% power=0.5W package=THT]
  R2 = Resistor [tolerance=±5% resistance=220 package="2512 [SMD]"]
  R3 = Rotary Potentiometer (Small) [maximum_resistance=10kΩ knob_status=50% power=0.5W package=THT]  # not connected
  R4 = Rotary Potentiometer (Small) [maximum_resistance=10kΩ knob_status=50% power=0.5W package=THT]  # not connected
  R5 = Rotary Potentiometer (Small) [maximum_resistance=10kΩ knob_status=50% power=0.5W package=THT]  # not connected
  R6 = Rotary Potentiometer (Small) [maximum_resistance=10kΩ knob_status=50% power=0.5W package=THT]  # not connected

nets:
  N1: Part1.A0, R1.wiper
  N2: Part1.GND, VCC1.-, C2.+, M1.POWER-, M1.INPUTG, R2.Pin_0
  N3: Part1.D11_PWM, R2.Pin_1
  N4: Part1.5V, M1.POWER+, R1.leg1, R1.leg2
  N5: Part1.VIN, VCC1.+
  N6: SP1.+, M1.LOUT-
  N7: SP1.-, M1.LOUT+
  N8: C2.-, M1.INPUTR

custom parts:
  PAM8403 Stereo Amplifier with Volume Control: PAM8403 stereo amplifier module with volume control Descriptive words Links: PAM8403 product datasheet
